# Fritzing sketch phase-shift (saved by Fritzing 0.9.4)
breadboards: 1

parts:
  C1 = Ceramic Capacitor [capacitance=1µF package="100 mil [THT, multilayer]"]
  R1 = Resistor [tolerance=±5% resistance=100k package=THT]

nets:
  N1: C1.0, R1.Pin_1

notes:
  Output
  Oscilloscope Channel B
  Ground
  Signal generator input and Oscilloscope Channel A
