# Fritzing sketch rdiv (saved by Fritzing 0.9.4)
breadboards: 1

parts:
  Part1 = Arduino Uno (Rev3)
  R2 = Resistor [tolerance=±5% resistance=1k package=THT]
  R1 = Resistor [tolerance=±5% resistance=1k package=THT]

nets:
  N1: Part1.5V, R1.Pin_1
  N2: Part1.GND, R2.Pin_0
  N3: R2.Pin_1, R1.Pin_0
