# Fritzing sketch twoservo (saved by Fritzing 0.9.4)
breadboards: 1

parts:
  Part1 = Arduino Uno (Rev3)
  U1 = POT [package=alps_pot]
  J1 = Dagu DGServo 9g header connector (female) [package=THT]
  J2 = Basic Servo
  J4 = Dagu DGServo 9g header connector (female) [package=THT]
  U2 = POT [package=alps_pot]
  J5 = Basic Servo

nets:
  N1: Part1.A0, U1.S
  N2: Part1.A1, U2.S
  N3: Part1.D9_PWM, J4.pulse, J5.pulse
  N4: Part1.D11_PWM/MOSI, J1.pulse, J2.pulse
  VCC: Part1.5V, U1.E, J1.Vcc, J2.vcc, J4.Vcc, U2.E, J5.vcc
  GND: Part1.GND, U1.A, J1.gnd, J2.gnd, J4.gnd, U2.A, J5.gnd
